# Fritzing sketch transistor tester (saved by Fritzing 0.9.9b)
breadboards: 1

parts:
  LCD1 = LCD screen
  test_button = Pushbutton [package="[THT]"]
  Arduino_Uno = Arduino Uno (Rev3)
  R1 = Resistor [tolerance=±1% resistance=680 power=0.25 package=THT]
  R2 = Resistor [tolerance=±1% resistance=680 power=0.25 package=THT]
  R3 = Resistor [tolerance=±1% resistance=680 power=0.25 package=THT]
  R4 = Resistor [tolerance=±1% resistance=470k power=0.25 package=THT]
  R5 = Resistor [tolerance=±1% resistance=470k power=0.25 package=THT]
  R6 = Resistor [tolerance=±1% resistance=470k power=0.25 package=THT]
  R7 = Resistor [tolerance=±5% resistance=1k power=0.25 package=THT]
  R8 = Resistor [tolerance=±5% resistance=10k power=0.25 package=THT]

nets:
  GND: LCD1.VSS, LCD1.R/W, LCD1.LED-, test_button.Pin_1, test_button.Pin_2, Arduino_Uno.GND, R7.Pin_0
  5V: LCD1.VDD, Arduino_Uno.5V, R8.Pin_1
  N1: LCD1.V0, R7.Pin_1
  N2: LCD1.RS, Arduino_Uno.D7
  N3: LCD1.E, Arduino_Uno.D6_PWM
  N4: LCD1.DB4, Arduino_Uno.D5_PWM
  N5: LCD1.DB5, Arduino_Uno.D4
  N6: LCD1.DB6, Arduino_Uno.D3_PWM
  N7: LCD1.DB7, Arduino_Uno.D2
  3.3V: LCD1.LED+, Arduino_Uno.3V3
  N8: test_button.Pin_3, test_button.Pin_4, Arduino_Uno.D1/TX, R8.Pin_0
  TP1: Arduino_Uno.A0, R1.Pin_1, R4.Pin_0
  TP2: Arduino_Uno.A1, R2.Pin_1, R5.Pin_0
  TP3: Arduino_Uno.A2, R3.Pin_1, R6.Pin_0
  N9: Arduino_Uno.D8, R1.Pin_0
  N10: Arduino_Uno.D9_PWM, R4.Pin_1
  N11: Arduino_Uno.D10_PWM/SS, R2.Pin_0
  N12: Arduino_Uno.D11_PWM/MOSI, R5.Pin_1
  N13: Arduino_Uno.D12/MISO, R3.Pin_0
  N14: Arduino_Uno.D13/SCK, R6.Pin_1
